// Logisim project chapter1.circ as structural Verilog: 16 circuits, main circuit OrNemo
// Or
module OrNemo (
  input  a,
  input  b,
  output ot
);

  wire nand_1_out, nand_2_out;

  nand nand_1 (nand_1_out, a, a);
  nand nand_2 (nand_2_out, b, b);
  nand nand_3 (ot, nand_1_out, nand_2_out);
endmodule

module Or16 (
  input  [15:0] a,
  input  [15:0] b,
  output [15:0] ot
);

  OrNemo ornemo_1 (.a(a[0]), .b(b[0]), .ot(ot[0]));
  OrNemo ornemo_2 (.a(a[1]), .b(b[1]), .ot(ot[1]));
  OrNemo ornemo_3 (.a(a[2]), .b(b[2]), .ot(ot[2]));
  OrNemo ornemo_4 (.a(a[3]), .b(b[3]), .ot(ot[3]));
  OrNemo ornemo_5 (.a(a[4]), .b(b[4]), .ot(ot[4]));
  OrNemo ornemo_6 (.a(a[5]), .b(b[5]), .ot(ot[5]));
  OrNemo ornemo_7 (.a(a[6]), .b(b[6]), .ot(ot[6]));
  OrNemo ornemo_8 (.a(a[7]), .b(b[7]), .ot(ot[7]));
  OrNemo ornemo_9 (.a(a[8]), .b(b[8]), .ot(ot[8]));
  OrNemo ornemo_10 (.a(a[9]), .b(b[9]), .ot(ot[9]));
  OrNemo ornemo_11 (.a(a[10]), .b(b[10]), .ot(ot[10]));
  OrNemo ornemo_12 (.a(a[11]), .b(b[11]), .ot(ot[11]));
  OrNemo ornemo_13 (.a(a[12]), .b(b[12]), .ot(ot[12]));
  OrNemo ornemo_14 (.a(a[13]), .b(b[13]), .ot(ot[13]));
  OrNemo ornemo_15 (.a(a[14]), .b(b[14]), .ot(ot[14]));
  OrNemo ornemo_16 (.a(a[15]), .b(b[15]), .ot(ot[15]));
endmodule

// 8W
module Or8Way (
  input  [7:0] in_1,
  output out_2
);

  wire ornemo_1_ot, ornemo_2_ot, ornemo_3_ot, ornemo_4_ot, ornemo_5_ot, ornemo_6_ot;

  OrNemo ornemo_1 (.a(in_1[0]), .b(in_1[1]), .ot(ornemo_1_ot));
  OrNemo ornemo_2 (.a(ornemo_1_ot), .b(in_1[2]), .ot(ornemo_2_ot));
  OrNemo ornemo_3 (.a(ornemo_2_ot), .b(in_1[3]), .ot(ornemo_3_ot));
  OrNemo ornemo_4 (.a(ornemo_3_ot), .b(in_1[4]), .ot(ornemo_4_ot));
  OrNemo ornemo_5 (.a(ornemo_4_ot), .b(in_1[5]), .ot(ornemo_5_ot));
  OrNemo ornemo_6 (.a(ornemo_5_ot), .b(in_1[6]), .ot(ornemo_6_ot));
  OrNemo ornemo_7 (.a(ornemo_6_ot), .b(in_1[7]), .ot(out_2));
endmodule

module Or16Way (
  input  [15:0] in_1,
  output out_2
);

  wire or8way_1_out_2, or8way_2_out_2;

  Or8Way or8way_1 (.in_1(in_1[7:0]), .out_2(or8way_1_out_2));
  Or8Way or8way_2 (.in_1(in_1[15:8]), .out_2(or8way_2_out_2));
  or or_1 (out_2, or8way_1_out_2, or8way_2_out_2);
endmodule

// Nemo
module AndNemo (
  input  a,
  input  b,
  output ot
);

  wire nand_1_out, nand_2_out;

  nand nand_1 (nand_1_out, a, b);
  nand nand_2 (nand_2_out, a, b);
  nand nand_3 (ot, nand_1_out, nand_2_out);
endmodule

module And16 (
  input  [15:0] a,
  input  [15:0] b,
  output [15:0] ot
);

  AndNemo andnemo_1 (.a(a[0]), .b(b[0]), .ot(ot[0]));
  AndNemo andnemo_2 (.a(a[1]), .b(b[1]), .ot(ot[1]));
  AndNemo andnemo_3 (.a(a[2]), .b(b[2]), .ot(ot[2]));
  AndNemo andnemo_4 (.a(a[3]), .b(b[3]), .ot(ot[3]));
  AndNemo andnemo_5 (.a(a[4]), .b(b[4]), .ot(ot[4]));
  AndNemo andnemo_6 (.a(a[5]), .b(b[5]), .ot(ot[5]));
  AndNemo andnemo_7 (.a(a[6]), .b(b[6]), .ot(ot[6]));
  AndNemo andnemo_8 (.a(a[7]), .b(b[7]), .ot(ot[7]));
  AndNemo andnemo_9 (.a(a[8]), .b(b[8]), .ot(ot[8]));
  AndNemo andnemo_10 (.a(a[9]), .b(b[9]), .ot(ot[9]));
  AndNemo andnemo_11 (.a(a[10]), .b(b[10]), .ot(ot[10]));
  AndNemo andnemo_12 (.a(a[11]), .b(b[11]), .ot(ot[11]));
  AndNemo andnemo_13 (.a(a[12]), .b(b[12]), .ot(ot[12]));
  AndNemo andnemo_14 (.a(a[13]), .b(b[13]), .ot(ot[13]));
  AndNemo andnemo_15 (.a(a[14]), .b(b[14]), .ot(ot[14]));
  AndNemo andnemo_16 (.a(a[15]), .b(b[15]), .ot(ot[15]));
endmodule

module NotNemo (
  input  i,
  output ot
);

  nand nand_1 (ot, i, i);
endmodule

// 16
module Not16 (
  input  [15:0] in_1,
  output [15:0] out_2
);

  NotNemo notnemo_1 (.i(in_1[0]), .ot(out_2[0]));
  NotNemo notnemo_2 (.i(in_1[1]), .ot(out_2[1]));
  NotNemo notnemo_3 (.i(in_1[2]), .ot(out_2[2]));
  NotNemo notnemo_4 (.i(in_1[3]), .ot(out_2[3]));
  NotNemo notnemo_5 (.i(in_1[4]), .ot(out_2[4]));
  NotNemo notnemo_6 (.i(in_1[5]), .ot(out_2[5]));
  NotNemo notnemo_7 (.i(in_1[6]), .ot(out_2[6]));
  NotNemo notnemo_8 (.i(in_1[7]), .ot(out_2[7]));
  NotNemo notnemo_9 (.i(in_1[8]), .ot(out_2[8]));
  NotNemo notnemo_10 (.i(in_1[9]), .ot(out_2[9]));
  NotNemo notnemo_11 (.i(in_1[10]), .ot(out_2[10]));
  NotNemo notnemo_12 (.i(in_1[11]), .ot(out_2[11]));
  NotNemo notnemo_13 (.i(in_1[12]), .ot(out_2[12]));
  NotNemo notnemo_14 (.i(in_1[13]), .ot(out_2[13]));
  NotNemo notnemo_15 (.i(in_1[14]), .ot(out_2[14]));
  NotNemo notnemo_16 (.i(in_1[15]), .ot(out_2[15]));
endmodule

module XorNemo (
  input  a,
  input  b,
  output ot
);

  wire andnemo_1_ot, andnemo_2_ot, notnemo_1_ot, notnemo_2_ot;

  NotNemo notnemo_1 (.i(b), .ot(notnemo_1_ot));
  NotNemo notnemo_2 (.i(a), .ot(notnemo_2_ot));
  AndNemo andnemo_1 (.a(a), .b(notnemo_1_ot), .ot(andnemo_1_ot));
  AndNemo andnemo_2 (.a(notnemo_2_ot), .b(b), .ot(andnemo_2_ot));
  OrNemo ornemo_1 (.a(andnemo_1_ot), .b(andnemo_2_ot), .ot(ot));
endmodule

module Mux (
  input  a,
  input  b,
  input  sel,
  output ot
);

  wire andnemo_1_ot, andnemo_2_ot, notnemo_1_ot;

  NotNemo notnemo_1 (.i(sel), .ot(notnemo_1_ot));
  AndNemo andnemo_1 (.a(a), .b(notnemo_1_ot), .ot(andnemo_1_ot));
  AndNemo andnemo_2 (.a(b), .b(sel), .ot(andnemo_2_ot));
  OrNemo ornemo_1 (.a(andnemo_1_ot), .b(andnemo_2_ot), .ot(ot));
endmodule

// 16
module Mux16 (
  input  [15:0] a,
  input  [15:0] b,
  input  sel,
  output [15:0] ot
);

  wire [15:0] and16_1_ot, and16_2_ot, not16_1_out_2;

  Not16 not16_1 (.in_1({16{sel}}), .out_2(not16_1_out_2));
  And16 and16_1 (.a(a), .b(not16_1_out_2), .ot(and16_1_ot));
  And16 and16_2 (.a(b), .b({16{sel}}), .ot(and16_2_ot));
  Or16 or16_1 (.a(and16_1_ot), .b(and16_2_ot), .ot(ot));
endmodule

// 4x16
module Mux4Way16 (
  input  [15:0] a,
  input  [15:0] b,
  input  [15:0] c,
  input  [15:0] d,
  input  [1:0] sel,
  output [15:0] ot
);

  wire [15:0] mux16_1_ot, mux16_2_ot;

  Mux16 mux16_1 (.a(a), .b(b), .sel(sel[0]), .ot(mux16_1_ot));
  Mux16 mux16_2 (.a(c), .b(d), .sel(sel[0]), .ot(mux16_2_ot));
  Mux16 mux16_3 (.a(mux16_1_ot), .b(mux16_2_ot), .sel(sel[1]), .ot(ot));
endmodule

module Mux8Way16 (
  input  [15:0] a,
  input  [15:0] b,
  input  [15:0] c,
  input  [15:0] d,
  input  [15:0] e,
  input  [15:0] f,
  input  [15:0] g,
  input  [15:0] h,
  input  [2:0] sel,
  output [15:0] ot
);

  wire [15:0] multiplexer_1_out, multiplexer_2_out;

  Multiplexer #(.select(2), .width(16)) multiplexer_1 (
    .in0(a), .in1(b), .in2(c), .in3(d), .out(multiplexer_1_out), .sel(sel[1:0]));
  Multiplexer #(.select(2), .width(16)) multiplexer_2 (
    .in0(e), .in1(f), .in2(g), .in3(h), .out(multiplexer_2_out), .sel(sel[1:0]));
  Multiplexer #(.width(16)) multiplexer_3 (.in0(multiplexer_1_out), .in1(multiplexer_2_out), .out(ot), .sel(sel[2]));
endmodule

module DMux (
  input  in_1,
  input  in_2,
  output out_3,
  output out_4
);

  wire notnemo_1_ot;

  NotNemo notnemo_1 (.i(in_2), .ot(notnemo_1_ot));
  AndNemo andnemo_1 (.a(in_1), .b(notnemo_1_ot), .ot(out_3));
  AndNemo andnemo_2 (.a(in_1), .b(in_2), .ot(out_4));
endmodule

module DMux4Way (
  input  i,
  input  [1:0] sel,
  output a,
  output b,
  output c,
  output d
);

  wire dmux_1_out_3, dmux_1_out_4;

  DMux dmux_1 (.in_1(i), .in_2(sel[1]), .out_3(dmux_1_out_3), .out_4(dmux_1_out_4));
  DMux dmux_2 (.in_1(dmux_1_out_3), .in_2(sel[0]), .out_3(a), .out_4(b));
  DMux dmux_3 (.in_1(dmux_1_out_4), .in_2(sel[0]), .out_3(c), .out_4(d));
endmodule

module DMux8Way (
  input  i,
  input  [2:0] sel,
  output a,
  output b,
  output c,
  output d,
  output e,
  output f,
  output g,
  output h
);

  wire dmux_1_out_3, dmux_1_out_4;

  DMux dmux_1 (.in_1(i), .in_2(sel[2]), .out_3(dmux_1_out_3), .out_4(dmux_1_out_4));
  DMux4Way dmux4way_1 (.i(dmux_1_out_3), .sel(sel[1:0]), .a(a), .b(b), .c(c), .d(d));
  DMux4Way dmux4way_2 (.i(dmux_1_out_4), .sel(sel[1:0]), .a(e), .b(f), .c(g), .d(h));
endmodule
