// Logisim project chapter2.circ as structural Verilog
module HalfAdder (
  input  a,
  input  b,
  output sum,
  output carry
);

  xor xor_1 (sum, a, b);
  and and_1 (carry, a, b);
endmodule

module FullAdder (
  input  a,
  input  b,
  input  c,
  output sum,
  output carry
);

  wire halfadder_1_carry, halfadder_1_sum, halfadder_2_carry;

  HalfAdder halfadder_1 (.a(b), .b(c), .sum(halfadder_1_sum), .carry(halfadder_1_carry));
  HalfAdder halfadder_2 (.a(a), .b(halfadder_1_sum), .sum(sum), .carry(halfadder_2_carry));
  or or_1 (carry, halfadder_2_carry, halfadder_1_carry);
endmodule

module Add16 (
  input  [15:0] a,
  input  [15:0] b,
  output [15:0] ot,
  output carry
);

  wire fulladder_1_carry, fulladder_2_carry, fulladder_3_carry, fulladder_4_carry, fulladder_5_carry,
       fulladder_6_carry, fulladder_7_carry, fulladder_8_carry, fulladder_9_carry, fulladder_10_carry,
       fulladder_11_carry, fulladder_12_carry, fulladder_13_carry, fulladder_14_carry, fulladder_15_carry;

  FullAdder fulladder_1 (.a(1'b0), .b(a[0]), .c(b[0]), .sum(ot[0]), .carry(fulladder_1_carry));
  FullAdder fulladder_2 (.a(fulladder_1_carry), .b(a[1]), .c(b[1]), .sum(ot[1]), .carry(fulladder_2_carry));
  FullAdder fulladder_3 (.a(fulladder_2_carry), .b(a[2]), .c(b[2]), .sum(ot[2]), .carry(fulladder_3_carry));
  FullAdder fulladder_4 (.a(fulladder_3_carry), .b(a[3]), .c(b[3]), .sum(ot[3]), .carry(fulladder_4_carry));
  FullAdder fulladder_5 (.a(fulladder_4_carry), .b(a[4]), .c(b[4]), .sum(ot[4]), .carry(fulladder_5_carry));
  FullAdder fulladder_6 (.a(fulladder_5_carry), .b(a[5]), .c(b[5]), .sum(ot[5]), .carry(fulladder_6_carry));
  FullAdder fulladder_7 (.a(fulladder_6_carry), .b(a[6]), .c(b[6]), .sum(ot[6]), .carry(fulladder_7_carry));
  FullAdder fulladder_8 (.a(fulladder_7_carry), .b(a[7]), .c(b[7]), .sum(ot[7]), .carry(fulladder_8_carry));
  FullAdder fulladder_9 (.a(fulladder_8_carry), .b(a[8]), .c(b[8]), .sum(ot[8]), .carry(fulladder_9_carry));
  FullAdder fulladder_10 (.a(fulladder_9_carry), .b(a[9]), .c(b[9]), .sum(ot[9]), .carry(fulladder_10_carry));
  FullAdder fulladder_11 (.a(fulladder_10_carry), .b(a[10]), .c(b[10]), .sum(ot[10]), .carry(fulladder_11_carry));
  FullAdder fulladder_12 (.a(fulladder_11_carry), .b(a[11]), .c(b[11]), .sum(ot[11]), .carry(fulladder_12_carry));
  FullAdder fulladder_13 (.a(fulladder_12_carry), .b(a[12]), .c(b[12]), .sum(ot[12]), .carry(fulladder_13_carry));
  FullAdder fulladder_14 (.a(fulladder_13_carry), .b(a[13]), .c(b[13]), .sum(ot[13]), .carry(fulladder_14_carry));
  FullAdder fulladder_15 (.a(fulladder_14_carry), .b(a[14]), .c(b[14]), .sum(ot[14]), .carry(fulladder_15_carry));
  FullAdder fulladder_16 (.a(fulladder_15_carry), .b(a[15]), .c(b[15]), .sum(ot[15]), .carry(carry));
endmodule

module Inc16 (
  input  [15:0] in_1,
  output [15:0] out_2
);

  Add16 add16_1 (.a(in_1), .b(16'h1), .ot(out_2));  // open: carry
endmodule

module ALU (
  input  zx,
  input  nx,
  input  zy,
  input  ny,
  input  f,
  input  no,
  input  [15:0] x,
  input  [15:0] y,
  output [15:0] ot,
  output zr,
  output ng
);

  wire or16way_1_out_2;
  wire [15:0] adder16_ot, and_1_out, and_2_out, multiplexer_1_out, multiplexer_2_out, multiplexer_3_out,
       multiplexer_4_out, multiplexer_5_out, not_1_out, not_3_out, not_4_out;

  Multiplexer #(.width(16)) multiplexer_1 (.in0(x), .in1({16{1'b0}}), .out(multiplexer_1_out), .sel(zx));
  Multiplexer #(.width(16)) multiplexer_2 (.in0(multiplexer_1_out), .in1(not_1_out), .out(multiplexer_2_out), .sel(nx));
  assign not_1_out = ~multiplexer_1_out;  // NOT_Gate not_1, 16 bits wide
  Multiplexer #(.width(16)) multiplexer_3 (.in0(y), .in1({16{1'b0}}), .out(multiplexer_3_out), .sel(zy));
  Or16Way or16way_1 (.in_1(ot), .out_2(or16way_1_out_2));
  not not_2 (zr, or16way_1_out_2);
  Multiplexer #(.width(16)) multiplexer_4 (.in0(multiplexer_3_out), .in1(not_3_out), .out(multiplexer_4_out), .sel(ny));
  assign not_3_out = ~multiplexer_3_out;  // NOT_Gate not_3, 16 bits wide
  assign and_1_out = multiplexer_2_out & multiplexer_4_out;  // AND_Gate and_1, 16 bits wide
  Add16 adder16 (.a(multiplexer_2_out), .b(multiplexer_4_out), .ot(adder16_ot));  // open: carry
  assign and_2_out = ot & 16'h8000;  // AND_Gate and_2, 16 bits wide
  Multiplexer #(.width(16)) multiplexer_5 (.in0(and_1_out), .in1(adder16_ot), .out(multiplexer_5_out), .sel(f));
  Or16Way or16way_2 (.in_1(and_2_out), .out_2(ng));
  Multiplexer #(.width(16)) multiplexer_6 (.in0(multiplexer_5_out), .in1(not_4_out), .out(ot), .sel(no));
  assign not_4_out = ~multiplexer_5_out;  // NOT_Gate not_4, 16 bits wide
endmodule

// 8W
module Or8Way (
  input  [7:0] in_1,
  output out_2
);

  wire or_1_out, or_2_out, or_3_out, or_4_out, or_5_out, or_6_out;

  or or_1 (or_1_out, in_1[0], in_1[1]);
  or or_2 (or_2_out, or_1_out, in_1[2]);
  or or_3 (or_3_out, or_2_out, in_1[3]);
  or or_4 (or_4_out, or_3_out, in_1[4]);
  or or_5 (or_5_out, or_4_out, in_1[5]);
  or or_6 (or_6_out, or_5_out, in_1[6]);
  or or_7 (out_2, or_6_out, in_1[7]);
endmodule

module Or16Way (
  input  [15:0] in_1,
  output out_2
);

  wire or8way_1_out_2, or8way_2_out_2;

  Or8Way or8way_1 (.in_1(in_1[7:0]), .out_2(or8way_1_out_2));
  Or8Way or8way_2 (.in_1(in_1[15:8]), .out_2(or8way_2_out_2));
  or or_1 (out_2, or8way_1_out_2, or8way_2_out_2);
endmodule
