// Logisim project chapter3a.circ as structural Verilog
module RSFF (
  input  R,
  input  S,
  output out_3,
  output out_4
);

  nor nor_1 (out_3, R, out_4);
  nor nor_2 (out_4, out_3, S);
endmodule

module DFF (
  input  load,
  input  i,
  output ot,
  output out_4
);

  wire and_1_out, and_2_out, not_1_out;

  not not_1 (not_1_out, i);
  and and_1 (and_1_out, not_1_out, load);
  and and_2 (and_2_out, load, i);
  nor nor_1 (ot, and_1_out, out_4);
  nor nor_2 (out_4, ot, and_2_out);
endmodule

module Register16 (
  input  load,
  input  [15:0] i,
  output [15:0] o
);

  D_Flip_Flop d_ff_1 (.D(i[0]), .clk(load), .Q(o[0]));  // open: Qn, preset, reset
  D_Flip_Flop d_ff_2 (.D(i[1]), .clk(load), .Q(o[1]));  // open: Qn, preset, reset
  D_Flip_Flop d_ff_3 (.D(i[2]), .clk(load), .Q(o[2]));  // open: Qn, preset, reset
  D_Flip_Flop d_ff_4 (.D(i[3]), .clk(load), .Q(o[3]));  // open: Qn, preset, reset
  D_Flip_Flop d_ff_5 (.D(i[4]), .clk(load), .Q(o[4]));  // open: Qn, preset, reset
  D_Flip_Flop d_ff_6 (.D(i[5]), .clk(load), .Q(o[5]));  // open: Qn, preset, reset
  D_Flip_Flop d_ff_7 (.D(i[6]), .clk(load), .Q(o[6]));  // open: Qn, preset, reset
  D_Flip_Flop d_ff_8 (.D(i[7]), .clk(load), .Q(o[7]));  // open: Qn, preset, reset
  D_Flip_Flop d_ff_9 (.D(i[8]), .clk(load), .Q(o[8]));  // open: Qn, preset, reset
  D_Flip_Flop d_ff_10 (.D(i[9]), .clk(load), .Q(o[9]));  // open: Qn, preset, reset
  D_Flip_Flop d_ff_11 (.D(i[10]), .clk(load), .Q(o[10]));  // open: Qn, preset, reset
  D_Flip_Flop d_ff_12 (.D(i[11]), .clk(load), .Q(o[11]));  // open: Qn, preset, reset
  D_Flip_Flop d_ff_13 (.D(i[12]), .clk(load), .Q(o[12]));  // open: Qn, preset, reset
  D_Flip_Flop d_ff_14 (.D(i[13]), .clk(load), .Q(o[13]));  // open: Qn, preset, reset
  D_Flip_Flop d_ff_15 (.D(i[14]), .clk(load), .Q(o[14]));  // open: Qn, preset, reset
  D_Flip_Flop d_ff_16 (.D(i[15]), .clk(load), .Q(o[15]));  // open: Qn, preset, reset
endmodule

module RAM8 (
  input  load,
  input  [15:0] i,
  input  [2:0] address,
  output [15:0] out_4
);

  wire demultiplexer_1_out0, demultiplexer_1_out1, demultiplexer_1_out2, demultiplexer_1_out3,
       demultiplexer_1_out4, demultiplexer_1_out5, demultiplexer_1_out6, demultiplexer_1_out7;
  wire [15:0] register_1_q, register_2_q, register_3_q, register_4_q, register_5_q, register_6_q,
       register_7_q, register_8_q;

  Demultiplexer #(.select(3)) demultiplexer_1 (
    .out0(demultiplexer_1_out0), .out1(demultiplexer_1_out1), .out2(demultiplexer_1_out2),
    .out3(demultiplexer_1_out3), .out4(demultiplexer_1_out4), .out5(demultiplexer_1_out5),
    .out6(demultiplexer_1_out6), .out7(demultiplexer_1_out7), .in(load), .sel(address));
  Register #(.width(16)) register_1 (.D(i), .clk(demultiplexer_1_out0), .Q(register_1_q));  // open: en, clr
  Register #(.width(16)) register_2 (.D(i), .clk(demultiplexer_1_out1), .Q(register_2_q));  // open: en, clr
  Register #(.width(16)) register_3 (.D(i), .clk(demultiplexer_1_out2), .Q(register_3_q));  // open: en, clr
  Register #(.width(16)) register_4 (.D(i), .clk(demultiplexer_1_out3), .Q(register_4_q));  // open: en, clr
  Register #(.width(16)) register_5 (.D(i), .clk(demultiplexer_1_out4), .Q(register_5_q));  // open: en, clr
  Register #(.width(16)) register_6 (.D(i), .clk(demultiplexer_1_out5), .Q(register_6_q));  // open: en, clr
  Register #(.width(16)) register_7 (.D(i), .clk(demultiplexer_1_out6), .Q(register_7_q));  // open: en, clr
  Register #(.width(16)) register_8 (.D(i), .clk(demultiplexer_1_out7), .Q(register_8_q));  // open: en, clr
  Multiplexer #(.select(3), .width(16)) multiplexer_1 (
    .in0(register_1_q), .in1(register_2_q), .in2(register_3_q), .in3(register_4_q), .in4(register_5_q),
    .in5(register_6_q), .in6(register_7_q), .in7(register_8_q), .out(out_4), .sel(address));
endmodule

module RAM64 (
  input  load,
  input  [15:0] i,
  input  [5:0] address,
  output [15:0] o
);

  wire demultiplexer_1_out0, demultiplexer_1_out1, demultiplexer_1_out2, demultiplexer_1_out3,
       demultiplexer_1_out4, demultiplexer_1_out5, demultiplexer_1_out6, demultiplexer_1_out7;
  wire [15:0] ram8_1_out_4, ram8_2_out_4, ram8_3_out_4, ram8_4_out_4, ram8_5_out_4, ram8_6_out_4,
       ram8_7_out_4, ram8_8_out_4;

  Demultiplexer #(.select(3)) demultiplexer_1 (
    .out0(demultiplexer_1_out0), .out1(demultiplexer_1_out1), .out2(demultiplexer_1_out2),
    .out3(demultiplexer_1_out3), .out4(demultiplexer_1_out4), .out5(demultiplexer_1_out5),
    .out6(demultiplexer_1_out6), .out7(demultiplexer_1_out7), .in(load), .sel(address[5:3]));
  RAM8 ram8_1 (.load(demultiplexer_1_out0), .i(i), .address(address[2:0]), .out_4(ram8_1_out_4));
  RAM8 ram8_2 (.load(demultiplexer_1_out1), .i(i), .address(address[2:0]), .out_4(ram8_2_out_4));
  RAM8 ram8_3 (.load(demultiplexer_1_out2), .i(i), .address(address[2:0]), .out_4(ram8_3_out_4));
  RAM8 ram8_4 (.load(demultiplexer_1_out3), .i(i), .address(address[2:0]), .out_4(ram8_4_out_4));
  RAM8 ram8_5 (.load(demultiplexer_1_out4), .i(i), .address(address[2:0]), .out_4(ram8_5_out_4));
  RAM8 ram8_6 (.load(demultiplexer_1_out5), .i(i), .address(address[2:0]), .out_4(ram8_6_out_4));
  RAM8 ram8_7 (.load(demultiplexer_1_out6), .i(i), .address(address[2:0]), .out_4(ram8_7_out_4));
  RAM8 ram8_8 (.load(demultiplexer_1_out7), .i(i), .address(address[2:0]), .out_4(ram8_8_out_4));
  Multiplexer #(.select(3), .width(16)) multiplexer_1 (
    .in0(ram8_1_out_4), .in1(ram8_2_out_4), .in2(ram8_3_out_4), .in3(ram8_4_out_4), .in4(ram8_5_out_4),
    .in5(ram8_6_out_4), .in6(ram8_7_out_4), .in7(ram8_8_out_4), .out(o), .sel(address[5:3]));
endmodule

module PC (
  input  inc,
  input  load,
  input  reset,
  input  [15:0] i,
  output [15:0] o
);

  wire and_1_out, clock_1_out, or_1_out, or_2_out;
  wire [15:0] adder_1_out, multiplexer_1_out, multiplexer_2_out;

  Multiplexer #(.width(16)) multiplexer_1 (.in0(i), .in1({16{1'b0}}), .out(multiplexer_1_out), .sel(reset));
  Clock clock_1 (.out(clock_1_out));
  Adder #(.width(16)) adder_1 (.a(16'h1), .b(o), .out(adder_1_out));  // open: cin, cout
  or or_1 (or_1_out, load, reset);
  Multiplexer #(.width(16)) multiplexer_2 (
    .in0(adder_1_out), .in1(multiplexer_1_out), .out(multiplexer_2_out), .sel(or_1_out));
  or or_2 (or_2_out, inc, or_1_out);
  and and_1 (and_1_out, clock_1_out, or_2_out);
  Register16 register16_1 (.load(and_1_out), .i(multiplexer_2_out), .o(o));
endmodule

module PC_Optimize (
  input  inc,
  input  load,
  input  reset,
  input  [15:0] in_4,
  output [15:0] out_5
);

  wire clock_1_out;
  wire [15:0] adder_1_out, multiplexer_1_out, multiplexer_2_out, multiplexer_3_out;

  Adder #(.width(16)) adder_1 (.a(16'h1), .b(out_5), .out(adder_1_out));  // open: cin, cout
  Multiplexer #(.width(16)) multiplexer_1 (.in0(out_5), .in1(adder_1_out), .out(multiplexer_1_out), .sel(inc));
  Multiplexer #(.width(16)) multiplexer_2 (.in0(multiplexer_1_out), .in1(in_4), .out(multiplexer_2_out), .sel(load));
  Clock clock_1 (.out(clock_1_out));
  Multiplexer #(.width(16)) multiplexer_3 (
    .in0(multiplexer_2_out), .in1({16{1'b0}}), .out(multiplexer_3_out), .sel(reset));
  Register16 register16_1 (.load(clock_1_out), .i(multiplexer_3_out), .o(out_5));
endmodule
