// Logisim project chapter5.circ as structural Verilog
module Memory (
  input  [15:0] keyboardIn,
  input  [15:0] i,
  input  load,
  input  [14:0] address,
  output [15:0] screenOut,
  output [15:0] o
);

  wire demultiplexer_1_out0, demultiplexer_1_out1, demultiplexer_1_out2, or_1_out;
  wire [15:0] DataMemory_dout, Keyboard_q;

  Demultiplexer #(.select(2)) demultiplexer_1 (
    .out0(demultiplexer_1_out0), .out1(demultiplexer_1_out1), .out2(demultiplexer_1_out2), .in(load),
    .sel(address[14:13]));  // open: out3
  or or_1 (or_1_out, demultiplexer_1_out0, demultiplexer_1_out1);
  RAM #(.addrWidth(14), .dataWidth(16)) DataMemory (
    .addr(address[13:0]), .we(or_1_out), .oe(or_1_out), .clk(or_1_out), .din(i), .dout(DataMemory_dout));
  RAM #(.addrWidth(13), .dataWidth(16)) Screen (
    .addr(address[12:0]), .we(demultiplexer_1_out2), .oe(demultiplexer_1_out2), .clk(demultiplexer_1_out2),
    .din(i), .dout(screenOut));
  Register #(.trigger("high"), .width(16)) Keyboard (.D(keyboardIn), .clk(1'b1), .Q(Keyboard_q));  // open: en, clr
  Multiplexer #(.select(2), .width(16)) multiplexer_1 (
    .in0(DataMemory_dout), .in1(DataMemory_dout), .in2(screenOut), .in3(Keyboard_q), .out(o),
    .sel(address[14:13]));
endmodule

module CPU (
  input  [15:0] instruction,
  input  [15:0] inM,
  input  reset,
  input  mClock,
  input  clock,
  output [15:0] outM,
  output writeM,
  output [14:0] addressM,
  output [14:0] pc
);

  wire alu_1_ng, alu_1_zr, and_1_out, and_2_out, and_3_out, and_4_out, and_5_out, and_6_out, and_7_out,
       not_1_out, not_2_out, or_1_out, or_2_out, or_3_out, or_4_out;
  wire [14:0] multiplexer_1_out;
  wire [15:0] DRegister_q, multiplexer_2_out, multiplexer_3_out;
  wire [15:15] ARegister_q, pc_optimize_1_o;

  Multiplexer #(.width(15)) multiplexer_1 (
    .in0({15{1'b0}}), .in1(instruction[14:0]),
    .out({multiplexer_1_out[14:4], writeM, multiplexer_1_out[2:0]}), .sel(instruction[15]));
  Multiplexer #(.width(16)) multiplexer_2 (.in0(outM), .in1(instruction), .out(multiplexer_2_out), .sel(not_1_out));
  not not_1 (not_1_out, instruction[15]);
  or or_1 (or_1_out, multiplexer_1_out[5], not_1_out);
  Register #(.width(16)) DRegister (.D(outM), .clk(and_1_out), .Q(DRegister_q));  // open: en, clr
  and and_1 (and_1_out, multiplexer_1_out[4], and_2_out);
  and and_2 (and_2_out, mClock, clock);
  Register #(.width(16)) ARegister (
    .D(multiplexer_2_out), .clk(and_3_out), .Q({ARegister_q[15], addressM}));  // open: en, clr
  and and_3 (and_3_out, or_1_out, and_4_out);
  and and_4 (and_4_out, mClock, clock);
  Multiplexer #(.width(16)) multiplexer_3 (
    .in0({ARegister_q[15], addressM}), .in1(inM), .out(multiplexer_3_out), .sel(multiplexer_1_out[12]));
  and and_5 (and_5_out, multiplexer_1_out[2], alu_1_ng);
  and and_6 (and_6_out, multiplexer_1_out[0], not_2_out);
  or or_2 (or_2_out, and_6_out, or_3_out);
  and and_7 (and_7_out, multiplexer_1_out[1], alu_1_zr);
  or or_3 (or_3_out, and_5_out, and_7_out);
  PC_Optimize pc_optimize_1 (
    .i({ARegister_q[15], addressM}), .inc(1'b1), .load(or_2_out), .reset(reset), .clock(clock),
    .o({pc_optimize_1_o[15], pc}));
  ALU alu_1 (
    .x(DRegister_q), .y(multiplexer_3_out), .zx(multiplexer_1_out[11]), .nx(multiplexer_1_out[10]),
    .zy(multiplexer_1_out[9]), .ny(multiplexer_1_out[8]), .f(multiplexer_1_out[7]),
    .no(multiplexer_1_out[6]), .ot(outM), .zr(alu_1_zr), .ng(alu_1_ng));
  or or_4 (or_4_out, alu_1_ng, alu_1_zr);
  not not_2 (not_2_out, or_4_out);
endmodule

module Computer (
  input  reset
);

  wire and_1_out, and_2_out, clock_1_out, clock_2_out, cpu_1_writem;
  wire [14:0] cpu_1_addressm, cpu_1_pc;
  wire [15:0] cpu_1_outm, InstrucitonMemory_data, ram_1_dout;

  ROM #(.addrWidth(15), .dataWidth(16)) InstrucitonMemory (.addr(cpu_1_pc), .data(InstrucitonMemory_data));
  Clock clock_1 (.out(clock_1_out));
  Clock #(.highDuration(2), .lowDuration(2)) clock_2 (.out(clock_2_out));
  CPU cpu_1 (
    .instruction(InstrucitonMemory_data), .inM(ram_1_dout), .reset(reset), .mClock(clock_1_out),
    .clock(clock_2_out), .outM(cpu_1_outm), .writeM(cpu_1_writem), .addressM(cpu_1_addressm), .pc(cpu_1_pc));
  and and_1 (and_1_out, cpu_1_writem, and_2_out);
  and and_2 (and_2_out, clock_1_out, clock_2_out);
  RAM #(.addrWidth(15), .dataWidth(16), .enables("line")) ram_1 (
    .addr(cpu_1_addressm), .we(and_1_out), .clk(and_1_out), .din(cpu_1_outm), .dout(ram_1_dout));

  // Notes on the sheet:
  //   contents of InstrucitonMemory (hex, n*v repeats v):
  //   2 ea88 0 fc10 15 e304 1 fc10 15 e304 0 fc88 fc10 15 e304 1 fc10 2 f088 a ea87 15 ea87
endmodule

module ComputerDebug (
  input  reset,
  output [15:0] x,
  output [15:0] y,
  output [15:0] out_4,
  output [14:0] address,
  output [15:0] out_6
);

  wire alu_1_ng, alu_1_zr, and_1_out, and_2_out, and_3_out, and_4_out, and_5_out, and_6_out, and_7_out,
       and_8_out, and_9_out, clock_1_out, clock_2_out, not_1_out, not_2_out, or_1_out, or_2_out, or_3_out,
       or_4_out;
  wire [14:0] multiplexer_1_out, pc_optimize_1_o;
  wire [15:0] InstrucitonMemory_data, multiplexer_2_out;
  wire [15:15] ARegister_q, pc_optimize_1_o_2;

  ROM #(.addrWidth(15), .dataWidth(16)) InstrucitonMemory (.addr(pc_optimize_1_o), .data(InstrucitonMemory_data));
  Multiplexer #(.width(15)) multiplexer_1 (
    .in0({15{1'b0}}), .in1(InstrucitonMemory_data[14:0]), .out(multiplexer_1_out),
    .sel(InstrucitonMemory_data[15]));
  not not_1 (not_1_out, InstrucitonMemory_data[15]);
  Multiplexer #(.width(16)) multiplexer_2 (
    .in0(out_4), .in1(InstrucitonMemory_data), .out(multiplexer_2_out), .sel(not_1_out));
  or or_1 (or_1_out, multiplexer_1_out[5], not_1_out);
  Clock clock_1 (.out(clock_1_out));
  Clock #(.highDuration(2), .lowDuration(2)) clock_2 (.out(clock_2_out));
  and and_1 (and_1_out, clock_1_out, clock_2_out);
  and and_2 (and_2_out, or_1_out, and_3_out);
  and and_3 (and_3_out, clock_1_out, clock_2_out);
  Register #(.width(16)) DRegister (.D(out_4), .clk(and_4_out), .Q(x));  // open: en, clr
  and and_4 (and_4_out, multiplexer_1_out[4], and_1_out);
  Register #(.width(16)) ARegister (
    .D(multiplexer_2_out), .clk(and_2_out), .Q({ARegister_q[15], address}));  // open: en, clr
  Multiplexer #(.width(16)) multiplexer_3 (
    .in0({ARegister_q[15], address}), .in1(out_6), .out(y), .sel(multiplexer_1_out[12]));
  and and_5 (and_5_out, multiplexer_1_out[0], not_2_out);
  and and_6 (and_6_out, multiplexer_1_out[1], alu_1_zr);
  and and_7 (and_7_out, multiplexer_1_out[2], alu_1_ng);
  or or_2 (or_2_out, and_7_out, and_6_out);
  or or_3 (or_3_out, and_5_out, or_2_out);
  PC_Optimize pc_optimize_1 (
    .i({ARegister_q[15], address}), .inc(1'b1), .load(or_3_out), .reset(reset), .clock(clock_2_out),
    .o({pc_optimize_1_o_2[15], pc_optimize_1_o}));
  and and_8 (and_8_out, clock_1_out, clock_2_out);
  and and_9 (and_9_out, and_8_out, multiplexer_1_out[3]);
  ALU alu_1 (
    .x(x), .y(y), .zx(multiplexer_1_out[11]), .nx(multiplexer_1_out[10]), .zy(multiplexer_1_out[9]),
    .ny(multiplexer_1_out[8]), .f(multiplexer_1_out[7]), .no(multiplexer_1_out[6]), .ot(out_4),
    .zr(alu_1_zr), .ng(alu_1_ng));
  or or_4 (or_4_out, alu_1_ng, alu_1_zr);
  not not_2 (not_2_out, or_4_out);
  RAM #(.addrWidth(15), .dataWidth(16), .enables("line")) DataMemory (
    .addr(address), .we(and_9_out), .clk(and_9_out), .din(out_4), .dout(out_6));

  // Notes on the sheet:
  //   contents of InstrucitonMemory (hex, n*v repeats v):
  //   2 ea88 0 fc10 15 e304 1 fc10 15 e304 0 fc88 fc10 15 e304 1 fc10 2 f088 a ea87 15 ea87
endmodule

// i
module Delay (
  input  i,
  output o
);

  wire not_1_out, not_2_out, not_3_out, not_4_out, not_5_out, not_6_out, not_7_out;

  not not_1 (not_1_out, i);
  not not_2 (not_2_out, not_1_out);
  not not_3 (not_3_out, not_2_out);
  not not_4 (not_4_out, not_3_out);
  not not_5 (not_5_out, not_4_out);
  not not_6 (not_6_out, not_5_out);
  not not_7 (not_7_out, not_6_out);
  not not_8 (o, not_7_out);
endmodule
